# Fritzing sketch Fritzing Schematic (saved by Fritzing 1.0.1rc)
breadboards: 1

parts:
  Mod1 = Raspberry Pi Pico
  PCB2 = RTC_DS1302_module

nets:
  N1: Mod1.pin_1, PCB2.RST
  N2: Mod1.pin_2, PCB2.DAT
  N3: Mod1.pin_3, Mod1.pin_8, Mod1.pin_13, Mod1.pin_18, Mod1.pin_23, Mod1.pin_28, Mod1.pin_33, Mod1.pin_38, Mod1.pin_42, PCB2.GND
  N4: Mod1.pin_4, PCB2.CLK
  N5: Mod1.pin_36, PCB2.VCC

custom parts:
  Raspberry Pi Pico: Raspberry Pi Pico. Based around the RP2040 microcontroller the Pico is a low cost microcontroller device bringing Raspberry Pi quality, cost, and easy of use to the microcontroller space. Jan 2021, Split part in to two versions: tht (this one) and SMD. This one will drill holes for a .1 in header in pcb to allow plugging in the module as well as providing pads to solder the module to the top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
  RTC_DS1302_module: Arduino module DS1302 SPI Real Time Clock
