# Fritzing sketch Fritzing Schematic (saved by Fritzing 1.0.1rc)
breadboards: 1

parts:
  Mod1 = Raspberry Pi Pico
  LED1 = smd LED [color="Red (633nm)" package="1206 [SMD]"]
  R1 = Resistor [tolerance=±5% power=0.25 resistance=220 package=THT]
  U1 = POT [knob_status=50% package=pot_mammoth]

nets:
  N1: Mod1.pin_1, LED1.anode
  N2: Mod1.pin_3, Mod1.pin_8, Mod1.pin_13, Mod1.pin_18, Mod1.pin_23, Mod1.pin_28, Mod1.pin_33, Mod1.pin_38, R1.Pin_0, U1.E
  N3: Mod1.pin_31, U1.A
  N4: Mod1.pin_36, U1.S
  N5: LED1.cathode, R1.Pin_1

custom parts:
  Raspberry Pi Pico: Raspberry Pi Pico. Based around the RP2040 microcontroller the Pico is a low cost microcontroller device bringing Raspberry Pi quality, cost, and easy of use to the microcontroller space. Jan 2021, Split part in to two versions: tht (this one) and SMD. This one will drill holes for a .1 in header in pcb to allow plugging in the module as well as providing pads to solder the module to the top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
