# Fritzing sketch Fritzing Schematic (saved by Fritzing 1.0.1rc)
breadboards: 1

parts:
  Mod1 = Raspberry Pi Pico
  LED1 = RGB LED - (4 legs) [package="5 mm [THT]"]
  R1 = Resistor [tolerance=±5% power=0.25 resistance=220 package=THT]
  R2 = Resistor [tolerance=±5% power=0.25 resistance=220 package=THT]
  R3 = Resistor [tolerance=±5% power=0.25 resistance=220 package=THT]
  U1 = POT [knob_status=50% package=pot_alpha_rv16af-20]
  U2 = POT [knob_status=50% package=pot_alpha_rv16af-20]
  U3 = POT [knob_status=50% package=pot_alpha_rv16af-20]

nets:
  N1: Mod1.pin_1, R1.Pin_0
  N2: Mod1.pin_2, R2.Pin_0
  N3: Mod1.pin_3, Mod1.pin_8, Mod1.pin_13, Mod1.pin_18, Mod1.pin_23, Mod1.pin_28, Mod1.pin_33, Mod1.pin_38, U1.A, U2.A, U3.A
  N4: Mod1.pin_4, R3.Pin_0
  N5: Mod1.pin_31, U3.S
  N6: Mod1.pin_32, U2.S
  N7: Mod1.pin_34, U1.S
  N8: Mod1.pin_36, LED1.common_anode, U1.E, U2.E, U3.E
  N9: LED1.red_cathode, R1.Pin_1
  N10: LED1.green_cathode, R2.Pin_1
  N11: LED1.blue_cathode, R3.Pin_1

custom parts:
  Raspberry Pi Pico: Raspberry Pi Pico. Based around the RP2040 microcontroller the Pico is a low cost microcontroller device bringing Raspberry Pi quality, cost, and easy of use to the microcontroller space. Jan 2021, Split part in to two versions: tht (this one) and SMD. This one will drill holes for a .1 in header in pcb to allow plugging in the module as well as providing pads to solder the module to the top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
